// Logisim project processor.circ as structural Verilog: 11 circuits, main circuit main
module _1_bit_adder (
  input  in_1,
  input  A,
  input  B,
  output Sum,
  output C_out
);

  wire and_1_out, and_2_out, and_3_out, xor_1_out;

  and and_1 (and_1_out, in_1, A);
  and and_2 (and_2_out, B, in_1);
  or or_1 (C_out, and_1_out, and_2_out, and_3_out);
  and and_3 (and_3_out, A, B);
  xor xor_1 (xor_1_out, B, A);
  xor xor_2 (Sum, xor_1_out, in_1);

  // Notes on the sheet:
  //   C-In
endmodule

module _4_bit_ripple (
  input  in_1,
  input  A1,
  input  B1,
  input  A2,
  input  B2,
  input  A3,
  input  B3,
  input  A4,
  input  B4,
  output out_10,
  output out_11,
  output out_12,
  output out_13,
  output out_14
);

  wire n1_bit_adder_1_c_out, n1_bit_adder_2_c_out, n1_bit_adder_3_c_out;

  _1_bit_adder u_1_bit_adder_1 (.A(A1), .B(B1), .in_1(in_1), .C_out(n1_bit_adder_1_c_out), .Sum(out_10));
  _1_bit_adder u_1_bit_adder_2 (
    .A(A2), .B(B2), .in_1(n1_bit_adder_1_c_out), .C_out(n1_bit_adder_2_c_out), .Sum(out_11));
  _1_bit_adder u_1_bit_adder_3 (
    .A(A3), .B(B3), .in_1(n1_bit_adder_2_c_out), .C_out(n1_bit_adder_3_c_out), .Sum(out_12));
  _1_bit_adder u_1_bit_adder_4 (.A(A4), .B(B4), .in_1(n1_bit_adder_3_c_out), .C_out(out_14), .Sum(out_13));
endmodule

module _4_bit_counter (
  input  Reset,
  input  Clock,
  input  Increment,
  output [3:0] out_4
);

  wire and_1_out;
  wire [3:0] multiplexer_1_out, n4_bit_ripple_1_out_10;

  _4_bit_ripple u_4_bit_ripple_1 (
    .A1(out_4[0]), .B1(1'b1), .A2(out_4[1]), .B2(1'b0), .A3(out_4[2]), .B3(1'b0), .A4(out_4[3]), .B4(1'b0),
    .in_1(1'b0), .out_10(n4_bit_ripple_1_out_10[0]), .out_11(n4_bit_ripple_1_out_10[1]),
    .out_12(n4_bit_ripple_1_out_10[2]), .out_13(n4_bit_ripple_1_out_10[3]));  // open: out_14
  and and_1 (and_1_out, Clock, Increment);
  Multiplexer #(.width(4)) multiplexer_1 (
    .in0(n4_bit_ripple_1_out_10), .in1(4'b0000), .out(multiplexer_1_out), .sel(Reset));  // open: en
  Register #(.width(4)) register_1 (.D(multiplexer_1_out), .Q(out_4), .clk(and_1_out));  // open: en, clr
endmodule

module game_logic (
  input  in_1,
  input  B,
  input  in_3,
  input  in_4,
  input  Reset,
  input  in_6,
  input  Go,
  output out_8,
  output [3:0] out_9
);

  wire and_1_out, and_2_out, and_3_out, and_4_out, and_5_out;

  and and_1 (and_1_out, ~in_1, ~B, ~in_3, ~in_4);  // AND_Gate
  and and_2 (and_2_out, ~in_1, ~B, in_3, in_4);  // AND_Gate
  and and_3 (and_3_out, out_8, Go);
  or or_1 (out_8, and_1_out, and_2_out, and_4_out, and_5_out);
  _4_bit_counter u_4_bit_counter_1 (.Clock(in_6), .Increment(and_3_out), .Reset(Reset), .out_4(out_9));
  and and_4 (and_4_out, in_1, B, in_3);
  and and_5 (and_5_out, in_1, ~B, ~in_4);  // AND_Gate

  // Notes on the sheet:
  //   A
  //   C
  //   D
endmodule

module _4_bit_alu (
  input  [1:0] in_1,
  input  in_2,
  input  [3:0] A,
  input  [3:0] B,
  output [3:0] out_5,
  output out_6,
  output Carry_Out
);

  wire and_1_out, and_2_out, and_3_out, and_4_out, n1_bit_adder_1_c_out, n1_bit_adder_1_sum,
       n1_bit_adder_2_c_out, n1_bit_adder_2_sum, n1_bit_adder_3_sum, n1_bit_adder_4_sum, or_1_out, or_2_out,
       or_3_out, or_4_out;

  _1_bit_adder u_1_bit_adder_1 (
    .A(A[0]), .B(B[0]), .in_1(in_2), .C_out(n1_bit_adder_1_c_out), .Sum(n1_bit_adder_1_sum));
  _1_bit_adder u_1_bit_adder_2 (
    .A(A[1]), .B(B[1]), .in_1(n1_bit_adder_1_c_out), .C_out(n1_bit_adder_2_c_out), .Sum(n1_bit_adder_2_sum));
  _1_bit_adder u_1_bit_adder_3 (
    .A(A[2]), .B(B[2]), .in_1(n1_bit_adder_2_c_out), .C_out(out_6), .Sum(n1_bit_adder_3_sum));
  _1_bit_adder u_1_bit_adder_4 (.A(A[3]), .B(B[3]), .in_1(out_6), .C_out(Carry_Out), .Sum(n1_bit_adder_4_sum));
  or or_1 (or_1_out, A[0], B[0]);
  and and_1 (and_1_out, A[0], B[0]);
  or or_2 (or_2_out, A[1], B[1]);
  and and_2 (and_2_out, A[1], B[1]);
  or or_3 (or_3_out, A[2], B[2]);
  and and_3 (and_3_out, A[2], B[2]);
  or or_4 (or_4_out, A[3], B[3]);
  and and_4 (and_4_out, A[3], B[3]);
  Multiplexer #(.select(2)) multiplexer_1 (
    .in0(or_1_out), .in1(and_1_out), .in2(n1_bit_adder_1_sum), .in3(n1_bit_adder_1_sum), .out(out_5[0]),
    .sel(in_1));  // open: en
  Multiplexer #(.select(2)) multiplexer_2 (
    .in0(or_2_out), .in1(and_2_out), .in2(n1_bit_adder_2_sum), .in3(n1_bit_adder_2_sum), .out(out_5[1]),
    .sel(in_1));  // open: en
  Multiplexer #(.select(2)) multiplexer_3 (
    .in0(or_3_out), .in1(and_3_out), .in2(n1_bit_adder_3_sum), .in3(n1_bit_adder_3_sum), .out(out_5[2]),
    .sel(in_1));  // open: en
  Multiplexer #(.select(2)) multiplexer_4 (
    .in0(or_4_out), .in1(and_4_out), .in2(n1_bit_adder_4_sum), .in3(n1_bit_adder_4_sum), .out(out_5[3]),
    .sel(in_1));  // open: en
endmodule

module _16_bit_alu (
  input  [4:0] in_1,
  input  [15:0] in_2,
  input  [15:0] in_3,
  output [15:0] out_4,
  output [3:0] Cond
);

  wire and_1_out, n4_bit_alu_1_carry_out, n4_bit_alu_2_carry_out, n4_bit_alu_3_carry_out, n4_bit_alu_4_out_6;
  wire [0:0] or_1_out;
  wire [15:0] multiplexer_1_out, not_1_out, not_2_out;

  assign not_1_out = ~in_3;  // NOT_Gate not_1, 16 bits wide
  Multiplexer #(.width(16)) multiplexer_1 (
    .in0(in_3), .in1(not_1_out), .out(multiplexer_1_out), .sel(and_1_out));  // open: en
  and and_1 (and_1_out, in_1[2], ~in_1[1], in_1[0]);  // AND_Gate
  _4_bit_alu u_4_bit_alu_1 (
    .A(in_2[3:0]), .B(multiplexer_1_out[3:0]), .in_2(and_1_out), .in_1({in_1[0], or_1_out[0]}),
    .Carry_Out(n4_bit_alu_1_carry_out), .out_5(out_4[3:0]));  // open: out_6
  _4_bit_alu u_4_bit_alu_2 (
    .A(in_2[7:4]), .B(multiplexer_1_out[7:4]), .in_2(n4_bit_alu_1_carry_out), .in_1({in_1[0], or_1_out[0]}),
    .Carry_Out(n4_bit_alu_2_carry_out), .out_5(out_4[7:4]));  // open: out_6
  _4_bit_alu u_4_bit_alu_3 (
    .A(in_2[11:8]), .B(multiplexer_1_out[11:8]), .in_2(n4_bit_alu_2_carry_out),
    .in_1({in_1[0], or_1_out[0]}), .Carry_Out(n4_bit_alu_3_carry_out), .out_5(out_4[11:8]));  // open: out_6
  _4_bit_alu u_4_bit_alu_4 (
    .A(in_2[15:12]), .B(multiplexer_1_out[15:12]), .in_2(n4_bit_alu_3_carry_out),
    .in_1({in_1[0], or_1_out[0]}), .Carry_Out(Cond[2]), .out_5({Cond[1], out_4[14:12]}),
    .out_6(n4_bit_alu_4_out_6));
  or or_1 (or_1_out[0], in_1[0], in_1[1]);
  assign not_2_out = ~{Cond[1], out_4[14:0]};  // NOT_Gate not_2, 16 bits wide
  xor xor_1 (Cond[0], Cond[2], n4_bit_alu_4_out_6);
  and and_2 (Cond[3], not_2_out[15], not_2_out[14], not_2_out[13], not_2_out[12], not_2_out[11], not_2_out[10], not_2_out[9], not_2_out[8], not_2_out[7], not_2_out[6], not_2_out[5], not_2_out[4], not_2_out[3], not_2_out[2], not_2_out[1], not_2_out[0]);

  assign out_4[15] = Cond[1];

  // Notes on the sheet:
  //   A
  //   B
  //   V
  //   N
  //   C
  //   z
endmodule

module Register_File (
  input  [2:0] B,
  input  [2:0] A,
  input  wen,
  input  [2:0] in_4,
  input  [15:0] in_5,
  input  in_6,
  input  clock,
  output [15:0] out_8,
  output [15:0] out_9,
  output [15:0] out_10
);

  wire and_1_out, demultiplexer_1_out0, demultiplexer_1_out1, demultiplexer_1_out2, demultiplexer_1_out3,
       demultiplexer_1_out4, demultiplexer_1_out5, demultiplexer_1_out6, demultiplexer_1_out7;
  wire [15:0] demultiplexer_2_out0, demultiplexer_2_out1, demultiplexer_2_out2, demultiplexer_2_out3,
       demultiplexer_2_out4, demultiplexer_2_out5, demultiplexer_2_out6, demultiplexer_2_out7, register_1_q,
       register_2_q, register_3_q, register_4_q, register_5_q, register_6_q, register_7_q, register_8_q;

  Demultiplexer #(.select(3), .disabled(0)) demultiplexer_1 (
    .out0(demultiplexer_1_out0), .out1(demultiplexer_1_out1), .out2(demultiplexer_1_out2),
    .out3(demultiplexer_1_out3), .out4(demultiplexer_1_out4), .out5(demultiplexer_1_out5),
    .out6(demultiplexer_1_out6), .out7(demultiplexer_1_out7), .in(and_1_out), .sel(in_4), .en(and_1_out));
  Demultiplexer #(.select(3), .width(16), .disabled(0)) demultiplexer_2 (
    .out0(demultiplexer_2_out0), .out1(demultiplexer_2_out1), .out2(demultiplexer_2_out2),
    .out3(demultiplexer_2_out3), .out4(demultiplexer_2_out4), .out5(demultiplexer_2_out5),
    .out6(demultiplexer_2_out6), .out7(demultiplexer_2_out7), .in(in_5), .sel(in_4), .en(and_1_out));
  and and_1 (and_1_out, wen, clock);
  Register #(.width(16)) register_1 (
    .D(demultiplexer_2_out0), .Q(register_1_q), .clk(demultiplexer_1_out0), .clr(in_6));  // open: en
  Register #(.width(16)) register_2 (
    .D(demultiplexer_2_out1), .Q(register_2_q), .clk(demultiplexer_1_out1), .clr(in_6));  // open: en
  Register #(.width(16)) register_3 (
    .D(demultiplexer_2_out2), .Q(register_3_q), .clk(demultiplexer_1_out2), .clr(in_6));  // open: en
  Register #(.width(16)) register_4 (
    .D(demultiplexer_2_out3), .Q(register_4_q), .clk(demultiplexer_1_out3), .clr(in_6));  // open: en
  Register #(.width(16)) register_5 (
    .D(demultiplexer_2_out4), .Q(register_5_q), .clk(demultiplexer_1_out4), .clr(in_6));  // open: en
  Register #(.width(16)) register_6 (
    .D(demultiplexer_2_out5), .Q(register_6_q), .clk(demultiplexer_1_out5), .clr(in_6));  // open: en
  Register #(.width(16)) register_7 (
    .D(demultiplexer_2_out6), .Q(register_7_q), .clk(demultiplexer_1_out6), .clr(in_6));  // open: en
  Register #(.width(16)) register_8 (
    .D(demultiplexer_2_out7), .Q(register_8_q), .clk(demultiplexer_1_out7), .clr(in_6));  // open: en
  Multiplexer #(.select(3), .width(16), .enable("false")) multiplexer_1 (
    .in0(register_1_q), .in1(register_2_q), .in2(register_3_q), .in3(register_4_q), .in4(register_5_q),
    .in5(register_6_q), .in6(register_7_q), .in7(register_8_q), .out(out_8), .sel(A));
  Multiplexer #(.select(3), .width(16), .enable("false")) multiplexer_2 (
    .in0(register_1_q), .in1(register_2_q), .in2(register_3_q), .in3(register_4_q), .in4(register_5_q),
    .in5(register_6_q), .in6(register_7_q), .in7(register_8_q), .out(out_9), .sel(in_4));
  Multiplexer #(.select(3), .width(16), .enable("false")) multiplexer_3 (
    .in0(register_1_q), .in1(register_2_q), .in2(register_3_q), .in3(register_4_q), .in4(register_5_q),
    .in5(register_6_q), .in6(register_7_q), .in7(register_8_q), .out(out_10), .sel(B));

  // Notes on the sheet:
  //   Travis Earley Te4
endmodule

module main (
  input  Reset,
  output Z,
  output [15:0] out_3,
  output C,
  output N,
  output V,
  output [3:0] out_7,
  output [15:0] out_8
);

  wire branch_control_1_pcsel, BRRequest, Clock_out, comparator_1_eq, comparator_2_gt, comparator_3_eq,
       comparator_4_eq, comparator_5_eq, MemRead, MemWrite, MovIs, not_1_out, not_3_out, or_1_out, RegWrite,
       UpdateCond;
  wire [1:0] ExtSel;
  wire [2:0] ALUBSrc, BranchType, MemToReg, RegA, RegB, RegW, ShiftOP;
  wire [4:0] ALUOP, Imm5;
  wire [7:0] Imm8;
  wire [10:0] Imm11;
  wire [15:0] ABus, AInt, AluOut, AOut, BBus, bit_extender_1_out, bit_extender_2_out, bit_extender_3_out,
       bit_extender_4_out, bit_extender_5_out, bit_extender_6_out, bit_extender_7_out, BOut, DataOut, Inst,
       IS, multiplexer_1_out, multiplexer_2_out, multiplexer_6_out, negator_1_out, NextPC, PC, PC_q, PCP0,
       PCP1, PCP8, PCP11, shifter_1_out_3, shifter_1_out_4, shifter_1_out_5, shifter_2_out_4;

  Clock Clock (.out(Clock_out));
  assign bit_extender_1_out = {{8{1'b0}}, Imm8};  // Bit_Extender bit_extender_1
  Register #(.width(16)) u_PC (.D(NextPC), .Q(PC_q), .clk(not_1_out), .clr(Reset));  // open: en
  Register #(.width(16)) CurrentPC (.D(PC_q), .Q(PC), .clk(Clock_out), .clr(Reset));  // open: en
  not not_1 (not_1_out, Clock_out);
  Shifter shifter_1 (
    .in_1(Imm5), .in_2(AOut), .out_3(shifter_1_out_3), .out_4(shifter_1_out_4), .out_5(shifter_1_out_5));
  Shifter shifter_2 (.in_1(5'b11000), .in_2(bit_extender_1_out), .out_4(shifter_2_out_4));  // open: out_3, out_5
  assign bit_extender_2_out = {{5{Imm11[10]}}, Imm11};  // Bit_Extender bit_extender_2
  assign bit_extender_3_out = {{8{Imm8[7]}}, Imm8};  // Bit_Extender bit_extender_3
  _16_bit_alu u_16_bit_alu_1 (.in_2(PC), .in_3(bit_extender_2_out), .out_4(PCP11), .in_1(5'b00001));  // open: Cond
  _16_bit_alu u_16_bit_alu_2 (.in_2(PC), .in_3(16'h1), .out_4(PCP1), .in_1(5'b00001));  // open: Cond
  _16_bit_alu u_16_bit_alu_3 (.in_2(PC), .in_3(bit_extender_3_out), .out_4(PCP8), .in_1(5'b00001));  // open: Cond
  _16_bit_alu u_16_bit_alu_4 (.in_2(PC), .in_3({16{1'b0}}), .out_4(PCP0), .in_1(5'b00001));  // open: Cond
  RAM #(.addrWidth(16), .dataWidth(16), .bus("asynch")) ram_1 (.addr(PC_q), .data(Inst), .clr(Reset));  // open: sel, ld
  Multiplexer #(.select(3), .width(16), .enable("false")) multiplexer_1 (
    .in0(AluOut), .in1(shifter_1_out_3), .in2(shifter_1_out_4), .in3(shifter_1_out_5), .in7(DataOut),
    .out(multiplexer_1_out), .sel(MemToReg));  // open: in4, in5, in6
  _16_bit_alu u_16_bit_alu_5 (.in_2(out_8), .in_3(shifter_2_out_4), .out_4(IS), .in_1({5{1'b0}}));  // open: Cond
  assign bit_extender_4_out = {{11{Imm5[4]}}, Imm5};  // Bit_Extender bit_extender_4
  assign bit_extender_5_out = {{8{Imm8[7]}}, Imm8};  // Bit_Extender bit_extender_5
  assign bit_extender_6_out = {{8{1'b0}}, Imm8};  // Bit_Extender bit_extender_6
  Multiplexer #(.width(16), .enable("false")) multiplexer_2 (
    .in0(multiplexer_1_out), .in1(IS), .out(multiplexer_2_out), .sel(MovIs));
  Negator #(.width(16)) negator_1 (.in(AOut), .out(negator_1_out));
  Comparator #(.width(5), .mode("unsigned")) comparator_1 (
    .a(5'b00110), .b(ALUOP), .eq(comparator_1_eq));  // open: gt, lt
  Comparator #(.width(5), .mode("unsigned")) comparator_2 (
    .a(ALUOP), .b(5'b10100), .gt(comparator_2_gt));  // open: eq, lt
  Comparator #(.width(5), .mode("unsigned")) comparator_3 (
    .a(ALUOP), .b(5'b10010), .eq(comparator_3_eq));  // open: gt, lt
  Comparator #(.width(5), .mode("unsigned")) comparator_4 (
    .a(ALUOP), .b(5'b10001), .eq(comparator_4_eq));  // open: gt, lt
  Multiplexer #(.width(16), .enable("false")) multiplexer_3 (
    .in0(multiplexer_2_out), .in1(negator_1_out), .out(out_3), .sel(comparator_1_eq));
  Multiplexer #(.width(16), .enable("false")) multiplexer_4 (.in0(AInt), .in1(out_8), .out(ABus), .sel(or_1_out));
  Register_File register_file_1 (
    .wen(RegWrite), .in_5(out_3), .out_8(AOut), .out_9(out_8), .out_10(BOut), .in_4(RegW), .A(RegA),
    .B(RegB), .in_6(Reset), .clock(Clock_out));
  Multiplexer #(.select(3), .width(16), .enable("false")) multiplexer_5 (
    .in0(BOut), .in1(bit_extender_4_out), .in2(bit_extender_5_out), .in4(bit_extender_6_out), .out(BBus),
    .sel(ALUBSrc));  // open: in3, in5, in6, in7
  or or_1 (or_1_out, comparator_2_gt, comparator_3_eq, comparator_4_eq);
  Multiplexer #(.select(2), .width(16), .enable("false")) multiplexer_6 (
    .in0(AOut), .in1(PCP11), .in2(PCP8), .in3(PCP0), .out(multiplexer_6_out), .sel(ExtSel));
  assign bit_extender_7_out = {{8{1'b0}}, Imm8};  // Bit_Extender bit_extender_7
  // NOT_Gate not_2 has open pins: in=Clock_out, out=open
  Branch_control branch_control_1 (
    .BranchType(BranchType), .Cond({Z, C, N, V}), .PCSel(branch_control_1_pcsel), .in_3(BRRequest));
  _16_bit_alu u_16_bit_alu_6 (.in_2(ABus), .in_3(BBus), .out_4(AluOut), .in_1(ALUOP), .Cond(out_7));
  Register #(.width(4)) CondCodes (.D(out_7), .en(UpdateCond), .Q({Z, C, N, V}), .clk(Clock_out), .clr(Reset));
  Comparator #(.width(5), .mode("unsigned")) comparator_5 (
    .a(ALUOP), .b(5'b10100), .eq(comparator_5_eq));  // open: gt, lt
  Multiplexer #(.width(16), .enable("false")) multiplexer_7 (
    .in0(AOut), .in1(bit_extender_7_out), .out(AInt), .sel(comparator_5_eq));
  Multiplexer #(.width(16), .enable("false")) multiplexer_8 (
    .in0(PCP1), .in1(multiplexer_6_out), .out(NextPC), .sel(branch_control_1_pcsel));
  not not_3 (not_3_out, Clock_out);
  RAM #(.addrWidth(16), .dataWidth(16), .bus("separate")) ram_2 (
    .addr(AluOut), .din(out_8), .data(DataOut), .str(MemWrite), .clk(not_3_out), .ld(MemRead), .clr(Reset));  // open: sel
  Decoder decoder_1 (
    .Instr(Inst), .ALUOp(ALUOP), .out_9(ALUBSrc), .out_10(BranchType), .out_11(ExtSel), .out_12(MemRead),
    .out_13(MemToReg), .out_14(MemWrite), .out_15(ShiftOP), .out_16(RegWrite), .out_17(UpdateCond),
    .out_18(BRRequest), .Imm11(Imm11), .Imm8(Imm8), .Imm5(Imm5), .RegW(RegW), .RegA(RegA), .RegB(RegB),
    .out_19(MovIs));

  // Other names for the same wires on the sheet: CondCodes[3:0] = {Z, C, N, V}; PCA[15:0] = AOut; WIn[15:0] = out_3;
  //   WOut[15:0] = out_8

  // Notes on the sheet:
  //   Travis Earley Te4 proj2
endmodule

module Branch_control (
  input  [2:0] BranchType,
  input  [3:0] Cond,
  input  in_3,
  output PCSel
);

  wire multiplexer_1_out, not_1_out, not_2_out, not_3_out, or_1_out, xor_1_out;

  not not_1 (not_1_out, Cond[3]);
  xor xor_1 (xor_1_out, Cond[0], Cond[1]);
  or or_1 (or_1_out, Cond[3], xor_1_out);
  not not_2 (not_2_out, or_1_out);
  not not_3 (not_3_out, xor_1_out);
  Multiplexer #(.select(3), .disabled(0)) multiplexer_1 (
    .in0(1'b1), .in1(not_2_out), .in2(Cond[3]), .in3(not_3_out), .in4(xor_1_out), .in5(not_1_out),
    .in6(or_1_out), .in7(1'b1), .out(multiplexer_1_out), .sel(BranchType));  // open: en
  and and_1 (PCSel, multiplexer_1_out, in_3);

  // Notes on the sheet:
  //   3 = Z
  //   2 = C
  //   1 = N
  //   0 = V
  //   1 = b.eq
  //   Z==1
endmodule

module Shifter (
  input  [4:0] in_1,
  input  [15:0] in_2,
  output [15:0] out_3,
  output [15:0] out_4,
  output [15:0] out_5
);

  wire [3:0] negator_1_out;
  wire [15:0] shifter_1_out, shifter_2_out, shifter_3_out, shifter_4_out, shifter_5_out;

  Negator #(.width(4)) negator_1 (.in(in_1[3:0]), .out(negator_1_out));
  Shifter_part #(.width(16), .shift("ar")) shifter_1 (.in(in_2), .\dist (in_1[3:0]), .out(shifter_1_out));
  Shifter_part #(.width(16), .shift("lr")) shifter_2 (.in(in_2), .\dist (in_1[3:0]), .out(shifter_2_out));
  Shifter_part #(.width(16)) shifter_3 (.in(in_2), .\dist (negator_1_out), .out(shifter_3_out));
  Shifter_part #(.width(16), .shift("rr")) shifter_4 (.in(in_2), .\dist (in_1[3:0]), .out(shifter_4_out));
  Shifter_part #(.width(16), .shift("rl")) shifter_5 (.in(in_2), .\dist (negator_1_out), .out(shifter_5_out));
  Multiplexer #(.width(16), .enable("false")) multiplexer_1 (
    .in0(shifter_1_out), .in1(shifter_3_out), .out(out_3), .sel(in_1[4]));
  Multiplexer #(.width(16), .enable("false")) multiplexer_2 (
    .in0(shifter_2_out), .in1(shifter_3_out), .out(out_4), .sel(in_1[4]));
  Multiplexer #(.width(16), .enable("false")) multiplexer_3 (
    .in0(shifter_4_out), .in1(shifter_5_out), .out(out_5), .sel(in_1[4]));
endmodule

module Decoder (
  input  [15:0] Instr,
  output [7:0] Imm8,
  output [4:0] Imm5,
  output [10:0] Imm11,
  output [2:0] RegW,
  output [2:0] RegA,
  output [2:0] RegB,
  output [4:0] ALUOp,
  output [2:0] out_9,
  output [2:0] out_10,
  output [1:0] out_11,
  output out_12,
  output [2:0] out_13,
  output out_14,
  output [2:0] out_15,
  output out_16,
  output out_17,
  output out_18,
  output out_19
);

  wire and_1_out, and_2_out, and_3_out, and_4_out, and_5_out, and_6_out, and_7_out, and_8_out, and_9_out,
       and_10_out, and_11_out, and_12_out, and_13_out, and_14_out, and_15_out, and_16_out, and_17_out,
       and_18_out, and_19_out, and_20_out, and_21_out, and_22_out, and_23_out, Ldw_out, Ldwi_out, shift_out,
       Stw_out, stwi_out;
  wire [0:0] B_out;
  wire [1:1] BR_out, call_out, Halt_out, not_1_out;
  wire [2:0] multiplexer_1_out, multiplexer_2_out;
  wire [2:2] ldw_2_out;

  and Ldw (Ldw_out, ~Instr[15], ~Instr[14], Instr[13], Instr[12], Instr[11]);  // AND_Gate
  and Ldwi (Ldwi_out, ~Instr[15], Instr[14], Instr[13], Instr[12], Instr[11]);  // AND_Gate
  and Stw (Stw_out, ~Instr[15], ~Instr[14], ~Instr[13], Instr[12], Instr[11]);  // AND_Gate
  and stwi (stwi_out, ~Instr[15], Instr[14], ~Instr[13], Instr[12], Instr[11]);  // AND_Gate
  and and_1 (and_1_out, ~Instr[15], ~Instr[13], ~Instr[12]);  // AND_Gate
  and and_2 (and_2_out, ~Instr[15], ~Instr[13], ~Instr[11]);  // AND_Gate
  and and_3 (and_3_out, ~Instr[15], Instr[13], Instr[12]);  // AND_Gate
  and and_4 (and_4_out, ~Instr[14], Instr[13], Instr[12]);  // AND_Gate
  and and_5 (and_5_out, Instr[15], ~Instr[14], ~Instr[13]);  // AND_Gate
  and and_6 (and_6_out, Instr[15], ~Instr[14], ~Instr[11]);  // AND_Gate
  and and_7 (and_7_out, ~Instr[15], ~Instr[14], ~Instr[12], Instr[11]);  // AND_Gate
  and and_8 (and_8_out, Instr[15], ~Instr[14], ~Instr[12], Instr[11]);  // AND_Gate
  and and_9 (and_9_out, Instr[15], ~Instr[14], Instr[13], Instr[11]);  // AND_Gate
  and and_10 (and_10_out, Instr[15], ~Instr[14], ~Instr[13], Instr[12], ~Instr[11]);  // AND_Gate
  and and_11 (and_11_out, Instr[15], ~Instr[14], ~Instr[12], ~Instr[11]);  // AND_Gate
  and and_12 (and_12_out, Instr[15], ~Instr[14], Instr[13], ~Instr[11]);  // AND_Gate
  and and_13 (and_13_out, ~Instr[14], ~Instr[12], Instr[11]);  // AND_Gate
  and and_14 (and_14_out, ~Instr[15], ~Instr[13], Instr[11]);  // AND_Gate
  and and_15 (and_15_out, ~Instr[15], Instr[14], ~Instr[13], ~Instr[11]);  // AND_Gate
  and and_16 (and_16_out, ~Instr[15], Instr[14], Instr[12], ~Instr[11]);  // AND_Gate
  and and_17 (and_17_out, Instr[15], Instr[14], ~Instr[13]);  // AND_Gate
  and and_18 (and_18_out, Instr[15], Instr[14], ~Instr[12]);  // AND_Gate
  and and_19 (and_19_out, Instr[15], Instr[14], ~Instr[11]);  // AND_Gate
  and and_20 (and_20_out, Instr[15], Instr[13], Instr[12], Instr[11]);
  and and_21 (and_21_out, ~Instr[15], ~Instr[14], Instr[13], ~Instr[12], ~Instr[11]);  // AND_Gate
  and and_22 (and_22_out, Instr[15], Instr[14], ~Instr[13], ~Instr[12], ~Instr[11]);  // AND_Gate
  and and_23 (and_23_out, ~Instr[15], ~Instr[14], Instr[13], ~Instr[12], ~Instr[11]);  // AND_Gate
  and and_24 (out_19, Instr[15], ~Instr[14], Instr[13], Instr[12], ~Instr[11]);  // AND_Gate
  and Arith (out_15[0], ~Instr[15], Instr[14], ~Instr[13], ~Instr[12], ~Instr[11]);  // AND_Gate
  and Logi (out_15[1], ~Instr[15], Instr[14], ~Instr[13], Instr[12], ~Instr[11]);  // AND_Gate
  and Roll (out_15[2], ~Instr[15], Instr[14], Instr[13], Instr[12], ~Instr[11]);  // AND_Gate
  // AND_Gate RegB has open pins: in0=Instr[15], in1=Instr[14], out=open
  or or_1 (out_12, Ldw_out, Ldwi_out);
  or or_2 (out_14, Stw_out, stwi_out);
  and Im5 (out_9[0], ~Instr[15], Instr[14]);  // AND_Gate
  or Im8S (out_9[1], and_8_out, and_9_out, and_10_out);
  or Im8Z (out_9[2], and_11_out, and_12_out);
  or shift (shift_out, and_15_out, and_16_out);
  and ldw_2 (ldw_2_out[2], ~Instr[15], Instr[13], Instr[12], Instr[11]);  // AND_Gate
  and call (call_out[1], Instr[15], ~Instr[14], Instr[13], Instr[12], Instr[11]);  // AND_Gate
  not not_1 (not_1_out[1], BR_out[1]);
  and BR (BR_out[1], ~Instr[15], ~Instr[14], Instr[13], ~Instr[12], ~Instr[11]);  // AND_Gate
  or B (B_out[0], and_17_out, and_18_out, and_19_out);
  and Halt (Halt_out[1], Instr[15], Instr[14], Instr[13], Instr[12], Instr[11]);
  // OR_Gate Uncond has open pins: in0=and_20_out, in1=and_21_out, in2=and_22_out, out=open
  // AND_Gate B_GT has open pins: in0=Instr[15], in1=Instr[14], in2=Instr[13], in3=Instr[12], in4=Instr[11], out=open
  // AND_Gate B_EQ has open pins: in0=Instr[15], in1=Instr[14], in2=Instr[13], in3=Instr[12], in4=Instr[11], out=open
  // AND_Gate B_GE has open pins: in0=Instr[15], in1=Instr[14], in2=Instr[13], in3=Instr[12], in4=Instr[11], out=open
  // AND_Gate B_LT has open pins: in0=Instr[15], in1=Instr[14], in2=Instr[13], in3=Instr[12], in4=Instr[11], out=open
  // AND_Gate B_NE has open pins: in0=Instr[15], in1=Instr[14], in2=Instr[13], in3=Instr[12], in4=Instr[11], out=open
  // AND_Gate B_LE has open pins: in0=Instr[15], in1=Instr[14], in2=Instr[13], in3=Instr[12], in4=Instr[11], out=open
  or Cond (out_17, and_13_out, and_14_out);
  Multiplexer #(.select(3), .width(3), .enable("false")) multiplexer_1 (
    .in0(3'b001), .in2(3'b010), .in6(3'b011), .out(multiplexer_1_out), .sel(Instr[13:11]));  // open: in1, in3, in4, in5, in7
  or or_3 (out_16, and_1_out, and_2_out, and_3_out, and_4_out, and_5_out, and_6_out, and_7_out);
  Multiplexer #(.width(3), .enable("false")) multiplexer_2 (
    .in0(3'b000), .in1(multiplexer_1_out), .out(multiplexer_2_out), .sel(shift_out));
  Multiplexer #(.width(3), .enable("false")) multiplexer_3 (
    .in0(Instr[13:11]), .in1(3'b111), .out(out_10), .sel(and_23_out));
  Multiplexer #(.width(3), .enable("false")) multiplexer_4 (
    .in0(multiplexer_2_out), .in1({3{ldw_2_out[2]}}), .out(out_13), .sel(ldw_2_out[2]));
  Multiplexer #(.select(4), .width(2), .enable("false")) multiplexer_5 (
    .in1({call_out[1], 1'b0}), .in2({2{not_1_out[1]}}), .in4({1'b0, B_out[0]}), .in8({2{Halt_out[1]}}),
    .out(out_11), .sel({Halt_out[1], B_out[0], BR_out[1], call_out[1]}));  // open: in0, in3, in5, in6, in7, in9, in10, in11, in12, in13, in14, in15
  or or_4 (out_18, Halt_out[1], B_out[0], BR_out[1], call_out[1]);

  assign ALUOp = Instr[15:11];
  assign Imm5 = Instr[4:0];
  assign Imm8 = Instr[7:0];
  assign Imm11 = Instr[10:0];
  assign RegA = Instr[7:5];
  assign RegB = Instr[4:2];
  assign RegW = Instr[10:8];

  // Other names for the same wires on the sheet: Instr_Num[4:0] = Instr[15:11]; ALUBSrc[2:0] = out_9;
  //   BranchType[2:0] = out_10; BRRequest = out_18; ExtSel[1:0] = out_11; MemRead = out_12; MemToReg[2:0] = out_13;
  //   MemWrite = out_14; RegWrite = out_16; ShiftOP[2:0] = out_15; UpdateCond = out_17
endmodule
